# Fritzing sketch Sketch (saved by Fritzing 0.9.2b)
circuit board: 6.9125cm x 5.57257cm
breadboards: 1

parts:
  Part1 = Arduino Uno (Rev3)
  RHT1 = Humidity and Temperature Sensor RHT03
  R1 = Resistor [tolerance=±5% resistance=10k package=THT]
  7_Segment_4_Digit_Display1 = 7-SEGMENT-4DIGIT common anode [part_number="5461BS - 5462BS" package=7-segment-4digit-anode]

nets:
  N1: Part1.A0, 7_Segment_4_Digit_Display1.C
  N2: Part1.D8, 7_Segment_4_Digit_Display1.D4
  N3: Part1.D9_PWM, 7_Segment_4_Digit_Display1.G
  N4: Part1.D10_PWM/SS, 7_Segment_4_Digit_Display1.DP
  N5: Part1.D11_PWM/MOSI, 7_Segment_4_Digit_Display1.D
  N6: Part1.D12/MISO, 7_Segment_4_Digit_Display1.E
  N7: Part1.D13/SCK, RHT1.Data-signal, R1.Pin_0
  N8: Part1.GND, RHT1.GND_2
  N9: Part1.D2, 7_Segment_4_Digit_Display1.B
  N10: Part1.D3_PWM, 7_Segment_4_Digit_Display1.D3
  N11: Part1.D4, 7_Segment_4_Digit_Display1.D2
  N12: Part1.D5_PWM, 7_Segment_4_Digit_Display1.F
  N13: Part1.D6_PWM, 7_Segment_4_Digit_Display1.A
  N14: Part1.D7, 7_Segment_4_Digit_Display1.D1
  3V3: Part1.3V3, RHT1.Vcc, R1.Pin_1

custom parts:
  7-SEGMENT-4DIGIT common anode: A 7 Segment 4 Digit common anode display, with decimal points
